# Fritzing sketch kalp led (saved by Fritzing 0.9.10b)
breadboards: 1

parts:
  Parça1 = Arduino Uno (Rev3)
  LED1 = LED - 3mm [color="Red (633nm)" current=0.030 package="3 mm [THT]"]  # not connected
  LED2 = LED - 3mm [color="Red (633nm)" current=0.030 package="3 mm [THT]"]  # not connected
  LED3 = LED - 3mm [color="Red (633nm)" current=0.030 package="3 mm [THT]"]  # not connected
  LED4 = LED - 3mm [color="Red (633nm)" current=0.030 package="3 mm [THT]"]
  LED5 = LED - 3mm [color="Red (633nm)" current=0.030 package="3 mm [THT]"]
  LED6 = LED - 3mm [color="Red (633nm)" current=0.030 package="3 mm [THT]"]  # not connected
  LED7 = LED - 3mm [color="Red (633nm)" current=0.030 package="3 mm [THT]"]  # not connected
  LED8 = LED - 3mm [color="Red (633nm)" current=0.030 package="3 mm [THT]"]  # not connected
  LED9 = LED - 3mm [color="Red (633nm)" current=0.030 package="3 mm [THT]"]  # not connected
  LED10 = LED - 3mm [color="Red (633nm)" current=0.030 package="3 mm [THT]"]  # not connected
  LED11 = LED - 3mm [color="Red (633nm)" current=0.030 package="3 mm [THT]"]  # not connected
  LED12 = LED - 3mm [color="Red (633nm)" current=0.030 package="3 mm [THT]"]  # not connected
  LED13 = LED - 3mm [color="Red (633nm)" current=0.030 package="3 mm [THT]"]  # not connected
  LED14 = LED - 3mm [color="Red (633nm)" current=0.030 package="3 mm [THT]"]  # not connected
  LED15 = LED - 3mm [color="Red (633nm)" current=0.030 package="3 mm [THT]"]  # not connected
  LED16 = LED - 3mm [color="Red (633nm)" current=0.030 package="3 mm [THT]"]  # not connected
  LED17 = LED - 3mm [color="Red (633nm)" current=0.030 package="3 mm [THT]"]  # not connected
  R1 = Resistor [tolerance=±5% resistance=220 package="0402 [SMD]"]  # not connected
  R2 = Resistor [tolerance=±5% resistance=220 package="0402 [SMD]"]
  R3 = Resistor [tolerance=±5% resistance=220 package="0402 [SMD]"]
  R4 = Resistor [tolerance=±5% resistance=220 package="0402 [SMD]"]
  R6 = Resistor [tolerance=±5% resistance=220 package="0402 [SMD]"]  # not connected
  R7 = Resistor [tolerance=±5% resistance=220 package="0402 [SMD]"]  # not connected
  R8 = Resistor [tolerance=±5% resistance=220 package="0402 [SMD]"]  # not connected
  R9 = Resistor [tolerance=±5% resistance=220 package="0402 [SMD]"]  # not connected
  R10 = Resistor [tolerance=±5% resistance=220 package="0402 [SMD]"]  # not connected
  R11 = Resistor [tolerance=±5% resistance=220 package="0402 [SMD]"]  # not connected
  R12 = Resistor [tolerance=±5% resistance=220 package="0402 [SMD]"]
  R14 = Resistor [tolerance=±5% resistance=220 package="0402 [SMD]"]
  R15 = Resistor [tolerance=±5% resistance=220 package="0402 [SMD]"]
  R16 = Resistor [tolerance=±5% resistance=220 package="0402 [SMD]"]
  R17 = Resistor [tolerance=±5% resistance=220 package="0402 [SMD]"]
  R18 = Resistor [tolerance=±5% resistance=220 package="0402 [SMD]"]  # not connected
  R19 = Resistor [tolerance=±5% resistance=220 package="0402 [SMD]"]

nets:
  N1: Parça1.D8, R16.Pin_0
  N2: Parça1.D9_PWM, R17.Pin_0
  N3: Parça1.D10_PWM/SS, R12.Pin_0
  N4: Parça1.D2, R3.Pin_0
  N5: Parça1.D3_PWM, R2.Pin_0
  N6: Parça1.D4, R4.Pin_0
  N7: Parça1.D5_PWM, R19.Pin_0
  N8: Parça1.D6_PWM, R14.Pin_0
  N9: Parça1.D7, R15.Pin_0
  N10: Parça1.VIN, LED4.cathode, LED5.cathode
